// Logisim project cpu.circ as structural Verilog: 19 circuits, main circuit main
// CPU
module main (
  input  [31:0] RS_READ_VALUE,
  input  [31:0] RI_READ_VALUE,
  input  [31:0] RD_READ_VALUE,
  input  [31:0] JC_READ_VALUE,
  input  [31:0] INSTRUCTION,
  input  CLOCK,
  output [4:0] RS,
  output [4:0] RI,
  output [4:0] RD,
  output [31:0] RD_WRITE_VALUE,
  output RD_WRITE_ENABLE,
  output [23:0] FETCH_ADDRESS
);

  wire IMMEDIATEMUX, JALENABLE, JUMPENABLE, JUMPTRUE, u_decode_1_immediateflag;
  wire [2:0] u_decode_1_jc;
  wire [3:0] OPCODE, u_decode_1_opcode;
  wire [4:0] u_decode_1_rd, u_decode_1_ri, u_decode_1_rs;
  wire [16:0] u_decode_1_imm;
  wire [23:0] adder_1_out, JUMPADDR, u_decode_1_addr;
  wire [31:0] bit_extender_1_out, IMM, multiplexer_1_out, multiplexer_2_out;

  not not_1 (RD_WRITE_ENABLE, JUMPENABLE);
  u_PC u_pc_1 (.JUMPADDR(JUMPADDR), .JUMPENABLE(JUMPENABLE), .JUMPTRUE(JUMPTRUE), .CLOCK(CLOCK), .PC(FETCH_ADDRESS));
  Multiplexer #(.width(32)) multiplexer_1 (
    .in0(RI_READ_VALUE), .in1(IMM), .out(multiplexer_1_out), .sel(IMMEDIATEMUX));  // open: en
  Adder #(.width(24)) adder_1 (.a(24'h1), .b(FETCH_ADDRESS), .out(adder_1_out));  // open: cin, cout
  u_DECODE u_decode_1 (
    .INSTRUCTION(INSTRUCTION), .OPCODE(u_decode_1_opcode), .IMMEDIATEFLAG(u_decode_1_immediateflag),
    .RD(u_decode_1_rd), .RS(u_decode_1_rs), .RI(u_decode_1_ri), .IMM(u_decode_1_imm), .JC(u_decode_1_jc),
    .ADDR(u_decode_1_addr));
  Multiplexer #(.width(32)) multiplexer_2 (
    .in0(multiplexer_1_out), .in1(bit_extender_1_out), .out(multiplexer_2_out), .sel(JALENABLE));  // open: en
  assign bit_extender_1_out = {{8{1'b0}}, adder_1_out};  // Bit_Extender bit_extender_1
  u_ALU u_alu_1 (.ALU_X(RS_READ_VALUE), .ALU_Y(multiplexer_2_out), .ALU_RESULT(RD_WRITE_VALUE), .ALU_CONTROL(OPCODE));
  u_CONTROL u_control_1 (
    .OPCODE(u_decode_1_opcode), .IMMEDIATEFLAG(u_decode_1_immediateflag), .RD(u_decode_1_rd),
    .RS(u_decode_1_rs), .RI(u_decode_1_ri), .IMM(u_decode_1_imm), .JC(u_decode_1_jc), .ADDR(u_decode_1_addr),
    .JC_VALUE(JC_READ_VALUE), .JUMPENABLE(JUMPENABLE), .JALENABLE(JALENABLE), .RI_VALUE(RI_READ_VALUE),
    .OPCODE_2(OPCODE), .IMMEDIATEMUX(IMMEDIATEMUX), .RD_2(RD), .RS_2(RS), .RI_2(RI), .IMM_2(IMM),
    .ADDR_2(JUMPADDR), .JUMPTRUE(JUMPTRUE));
  u_MEM u_mem_1 ();  // open: ADDRESS, WORD_MODE, MEM_WRITE, DATA_IN, CLOCK, DATA_OUT

  // Other names for the same wires on the sheet: CLK = CLOCK; FETCHPC[23:0] = FETCH_ADDRESS; JC[31:0] = JC_READ_VALUE;
  //   RD_WRITE[31:0] = RD_WRITE_VALUE; RI_CONTROL[31:0] = RI_READ_VALUE

  // Notes on the sheet:
  //   Did not implement Data memory yet. All results go to RD for now
  //   This is here as a placeholder until we actually implement jump conditions
endmodule

module u_ALU (
  input  [31:0] ALU_X,
  input  [31:0] ALU_Y,
  input  [3:0] ALU_CONTROL,
  output [31:0] ALU_RESULT
);

  wire [31:0] ADD, AND, DIV, MUL, OR, REV, SL, SR, STU, SUB, XOR;

  u_ALU_ADD u_alu_add_1 (.ALU_X(ALU_X), .ALU_Y(ALU_Y), .RESULT(ADD));
  u_ALU_SUB u_alu_sub_1 (.ALU_X(ALU_X), .ALU_Y(ALU_Y), .RESULT(SUB));
  u_ALU_SL u_alu_sl_1 (.ALU_X(ALU_X), .ALU_Y(ALU_Y), .RESULT(SL));
  u_ALU_SR u_alu_sr_1 (.ALU_X(ALU_X), .ALU_Y(ALU_Y), .RESULT(SR));
  u_ALU_AND u_alu_and_1 (.ALU_X(ALU_X), .ALU_Y(ALU_Y), .RESULT(AND));
  u_ALU_OR u_alu_or_1 (.ALU_X(ALU_X), .ALU_Y(ALU_Y), .RESULT(OR));
  // u_ALU_REV u_alu_rev_1: pin names not known; wires that end beside it: ALU_Y, ALU_X, REV
  u_ALU_XOR u_alu_xor_1 (.ALU_X(ALU_X), .ALU_Y(ALU_Y), .RESULT(XOR));
  u_ALU_MUL u_alu_mul_1 (.ALU_X(ALU_X), .ALU_Y(ALU_Y), .RESULT(MUL));
  u_ALU_DIVIDE u_alu_divide_1 (.ALU_X(ALU_X), .ALU_Y(ALU_Y), .RESULT(DIV));
  u_ALU_STU u_alu_stu_1 (.ALU_X(ALU_X), .ALU_Y(ALU_Y), .RESULT(STU));
  Multiplexer #(.select(4), .width(32)) multiplexer_1 (
    .in0(SL), .in1(SR), .in2(AND), .in3(OR), .in4(REV), .in5(XOR), .in6(ADD), .in7(SUB), .in8(MUL),
    .in9(DIV), .in14(STU), .out(ALU_RESULT), .sel(ALU_CONTROL));  // open: in10, in11, in12, in13, in15, en

  // Notes on the sheet:
  //   Very simple ALU for now. Calculating all possible operations? Is this a performance lag?
endmodule

// Data Memory
module u_MEM (
  input  [24:0] ADDRESS,
  input  WORD_MODE,
  input  MEM_WRITE,
  input  [31:0] DATA_IN,
  input  CLOCK,
  output [31:0] DATA_OUT
);

  RAM #(.addrWidth(24), .dataWidth(16)) ram_1 ();  // open: addr, data, sel, clk, ld, clr
  RAM #(.addrWidth(24), .dataWidth(16)) ram_2 ();  // open: addr, data, sel, clk, ld, clr

  // Notes on the sheet:
  //   Feel free to use this component, or not, however you want!
  //   You might use the word mode input to differentiate LW/SW from LH/SH.
  //   However, you *SHOULD* use 2 RAM modules, one for even addresses and one for odd addresses.
endmodule

module u_ALU_REV (
  input  [31:0] INPUT,
  input  [4:0] REVERSE_AMOUNT,
  output [31:0] OUTPUT
);


  // Notes on the sheet:
  //   Feel free to use this component, or not, however you want!
endmodule

module u_DECODE (
  input  [31:0] INSTRUCTION,
  output [3:0] OPCODE,
  output IMMEDIATEFLAG,
  output [4:0] RD,
  output [4:0] RS,
  output [4:0] RI,
  output [16:0] IMM,
  output [2:0] JC,
  output [23:0] ADDR
);


  assign ADDR = INSTRUCTION[23:0];
  assign IMM = INSTRUCTION[16:0];
  assign IMMEDIATEFLAG = INSTRUCTION[27];
  assign JC = INSTRUCTION[26:24];
  assign OPCODE = INSTRUCTION[31:28];
  assign RD = INSTRUCTION[26:22];
  assign RI = INSTRUCTION[4:0];
  assign RS = INSTRUCTION[21:17];

  // Other names for the same wires on the sheet: ADDRT[23:0] = INSTRUCTION[23:0];
  //   IMMEDIATET[16:0] = INSTRUCTION[16:0]; INSTRUCT[31:0] = INSTRUCTION; RIT[4:0] = INSTRUCTION[4:0];
  //   RST[4:0] = INSTRUCTION[21:17]; RDT[4:0] = INSTRUCTION[26:22]; JCT[2:0] = INSTRUCTION[26:24];
  //   IMMEDIATEFLAGT = INSTRUCTION[27]; OPCODET[3:0] = INSTRUCTION[31:28]
endmodule

module u_CONTROL (
  input  [3:0] OPCODE,
  input  IMMEDIATEFLAG,
  input  [4:0] RD,
  input  [4:0] RS,
  input  [4:0] RI,
  input  [16:0] IMM,
  input  [2:0] JC,
  input  [23:0] ADDR,
  input  [31:0] RI_VALUE,
  input  [31:0] JC_VALUE,
  output JUMPENABLE,
  output [3:0] OPCODE_2,
  output IMMEDIATEMUX,
  output [4:0] RD_2,
  output [4:0] RS_2,
  output JALENABLE,
  output [4:0] RI_2,
  output [31:0] IMM_2,
  output [23:0] ADDR_2,
  output JUMPTRUE
);

  wire and_2_out, EQ___GT, EQ___LT, EQZ, GTZ, LQZ, not_1_out, not_2_out;

  Multiplexer #(.width(24)) multiplexer_1 (
    .in0(RI_VALUE[23:0]), .in1(ADDR), .out(ADDR_2), .sel(IMMEDIATEFLAG));  // open: en
  u_SIGNEXTEND17 u_signextend17_1 (.IMMEDIATE17(IMM), .IMMEDIATE32(IMM_2));
  Multiplexer #(.width(5)) multiplexer_2 (.in0(RD), .in1(5'b00110), .out(RD_2), .sel(JALENABLE));  // open: en
  not not_1 (not_1_out, EQZ);
  Multiplexer #(.select(3)) multiplexer_3 (
    .in0(1'b1), .in1(GTZ), .in2(EQZ), .in3(LQZ), .in4(EQ___LT), .in5(not_1_out), .in6(EQ___GT), .in7(1'b1),
    .out(JUMPTRUE), .sel(JC));  // open: en
  or or_1 (EQ___LT, EQZ, LQZ);
  or or_2 (EQ___GT, EQZ, GTZ);
  Comparator #(.width(32)) comparator_1 (.a(JC_VALUE), .b({32{1'b0}}), .gt(GTZ), .eq(EQZ), .lt(LQZ));
  and and_1 (JUMPENABLE, and_2_out, not_2_out);
  and and_2 (and_2_out, OPCODE[3], OPCODE[2], OPCODE[1], OPCODE[0]);
  not not_2 (not_2_out, JALENABLE);
  Comparator #(.width(3)) comparator_2 (.a(3'b111), .b(JC), .eq(JALENABLE));  // open: gt, lt

  assign IMMEDIATEMUX = IMMEDIATEFLAG;
  assign OPCODE_2 = OPCODE;
  assign RI_2 = RI;
  assign RS_2 = RS;

  // Other names for the same wires on the sheet: IMMEDIATE = IMMEDIATEFLAG; JAL = JALENABLE;
  //   RI_VALUE_t[23:0] = RI_VALUE[23:0]

  // Notes on the sheet:
  //   Very Simple for now. Only considering R-Type instructions
  //   Always sign extend. We can easily extract the actual immediate by getting lower 17 bits
  //   All Jump operations and conditions will be included in CONTROL
endmodule

module u_PC (
  input  JUMPENABLE,
  input  JUMPTRUE,
  input  [23:0] JUMPADDR,
  input  CLOCK,
  output [23:0] PC
);

  wire and_1_out;
  wire [23:0] multiplexer_1_out, NEXTPC;

  and and_1 (and_1_out, JUMPENABLE, JUMPTRUE);
  Multiplexer #(.width(24)) multiplexer_1 (
    .in0(NEXTPC), .in1(JUMPADDR), .out(multiplexer_1_out), .sel(and_1_out));  // open: en
  Register #(.width(24)) u_PC (.D(multiplexer_1_out), .Q(PC), .clk(CLOCK));  // open: en, clr
  Adder #(.width(24)) adder_1 (.a(24'h1), .b(PC), .out(NEXTPC));  // open: cin, cout
endmodule

module u_SIGNEXTEND17 (
  input  [16:0] IMMEDIATE17,
  output [31:0] IMMEDIATE32
);

  assign IMMEDIATE32 = {{15{IMMEDIATE17[16]}}, IMMEDIATE17};  // Bit_Extender bit_extender_1
endmodule

module u_ALU_ADD (
  input  [31:0] ALU_X,
  input  [31:0] ALU_Y,
  output [31:0] RESULT
);

  Adder #(.width(32)) adder_1 (.a(ALU_X), .b(ALU_Y), .out(RESULT));  // open: cin, cout
endmodule

module u_ALU_SUB (
  input  [31:0] ALU_X,
  input  [31:0] ALU_Y,
  output [31:0] RESULT
);

  Subtractor #(.width(32)) subtractor_1 (.a(ALU_X), .b(ALU_Y), .out(RESULT));  // open: bin, bout
endmodule

module u_ALU_MUL (
  input  [31:0] ALU_X,
  input  [31:0] ALU_Y,
  output [31:0] RESULT
);

  Multiplier #(.width(32)) multiplier_1 (.a(ALU_X), .b(ALU_Y), .out(RESULT));  // open: cin, cout
endmodule

module u_ALU_SL (
  input  [31:0] ALU_X,
  input  [31:0] ALU_Y,
  output [31:0] RESULT
);

  wire [31:0] CONT, CONT_2, multiplexer_1_out, multiplexer_2_out, u_alu_sl_shiftoneleft_1_result,
       u_alu_sl_shiftoneleft_2_result, u_alu_sl_shiftoneleft_3_result, u_alu_sl_shiftoneleft_4_result,
       u_alu_sl_shiftoneleft_5_result, u_alu_sl_shiftoneleft_6_result, u_alu_sl_shiftoneleft_7_result,
       u_alu_sl_shiftoneleft_8_result, u_alu_sl_shiftoneleft_9_result, u_alu_sl_shiftoneleft_10_result,
       u_alu_sl_shiftoneleft_11_result, u_alu_sl_shiftoneleft_12_result, u_alu_sl_shiftoneleft_13_result,
       u_alu_sl_shiftoneleft_14_result, u_alu_sl_shiftoneleft_15_result, u_alu_sl_shiftoneleft_16_result,
       u_alu_sl_shiftoneleft_17_result, u_alu_sl_shiftoneleft_18_result, u_alu_sl_shiftoneleft_19_result,
       u_alu_sl_shiftoneleft_20_result, u_alu_sl_shiftoneleft_21_result, u_alu_sl_shiftoneleft_22_result,
       u_alu_sl_shiftoneleft_23_result, u_alu_sl_shiftoneleft_24_result, u_alu_sl_shiftoneleft_25_result,
       u_alu_sl_shiftoneleft_26_result, u_alu_sl_shiftoneleft_27_result, u_alu_sl_shiftoneleft_28_result,
       u_alu_sl_shiftoneleft_29_result, u_alu_sl_shiftoneleft_30_result, u_alu_sl_shiftoneleft_31_result;

  u_ALU_SL_SHIFTONELEFT u_alu_sl_shiftoneleft_1 (.VALTOSHIFT(CONT), .RESULT(u_alu_sl_shiftoneleft_1_result));
  u_ALU_SL_SHIFTONELEFT u_alu_sl_shiftoneleft_2 (
    .VALTOSHIFT(u_alu_sl_shiftoneleft_1_result), .RESULT(u_alu_sl_shiftoneleft_2_result));
  u_ALU_SL_SHIFTONELEFT u_alu_sl_shiftoneleft_3 (
    .VALTOSHIFT(u_alu_sl_shiftoneleft_4_result), .RESULT(u_alu_sl_shiftoneleft_3_result));
  u_ALU_SL_SHIFTONELEFT u_alu_sl_shiftoneleft_4 (.VALTOSHIFT(CONT_2), .RESULT(u_alu_sl_shiftoneleft_4_result));
  u_ALU_SL_SHIFTONELEFT u_alu_sl_shiftoneleft_5 (.VALTOSHIFT(ALU_X), .RESULT(u_alu_sl_shiftoneleft_5_result));
  u_ALU_SL_SHIFTONELEFT u_alu_sl_shiftoneleft_6 (
    .VALTOSHIFT(u_alu_sl_shiftoneleft_7_result), .RESULT(u_alu_sl_shiftoneleft_6_result));
  u_ALU_SL_SHIFTONELEFT u_alu_sl_shiftoneleft_7 (
    .VALTOSHIFT(u_alu_sl_shiftoneleft_2_result), .RESULT(u_alu_sl_shiftoneleft_7_result));
  u_ALU_SL_SHIFTONELEFT u_alu_sl_shiftoneleft_8 (
    .VALTOSHIFT(u_alu_sl_shiftoneleft_9_result), .RESULT(u_alu_sl_shiftoneleft_8_result));
  u_ALU_SL_SHIFTONELEFT u_alu_sl_shiftoneleft_9 (
    .VALTOSHIFT(u_alu_sl_shiftoneleft_3_result), .RESULT(u_alu_sl_shiftoneleft_9_result));
  Multiplexer #(.width(32)) multiplexer_1 (
    .in0(ALU_X), .in1(u_alu_sl_shiftoneleft_5_result), .out(multiplexer_1_out), .sel(ALU_Y[0]));  // open: en
  u_ALU_SL_SHIFTONELEFT u_alu_sl_shiftoneleft_10 (
    .VALTOSHIFT(u_alu_sl_shiftoneleft_11_result), .RESULT(u_alu_sl_shiftoneleft_10_result));
  u_ALU_SL_SHIFTONELEFT u_alu_sl_shiftoneleft_11 (
    .VALTOSHIFT(u_alu_sl_shiftoneleft_6_result), .RESULT(u_alu_sl_shiftoneleft_11_result));
  u_ALU_SL_SHIFTONELEFT u_alu_sl_shiftoneleft_12 (
    .VALTOSHIFT(u_alu_sl_shiftoneleft_8_result), .RESULT(u_alu_sl_shiftoneleft_12_result));
  u_ALU_SL_SHIFTONELEFT u_alu_sl_shiftoneleft_13 (
    .VALTOSHIFT(u_alu_sl_shiftoneleft_12_result), .RESULT(u_alu_sl_shiftoneleft_13_result));
  u_ALU_SL_SHIFTONELEFT u_alu_sl_shiftoneleft_14 (
    .VALTOSHIFT(multiplexer_1_out), .RESULT(u_alu_sl_shiftoneleft_14_result));
  u_ALU_SL_SHIFTONELEFT u_alu_sl_shiftoneleft_15 (
    .VALTOSHIFT(u_alu_sl_shiftoneleft_10_result), .RESULT(u_alu_sl_shiftoneleft_15_result));
  u_ALU_SL_SHIFTONELEFT u_alu_sl_shiftoneleft_16 (
    .VALTOSHIFT(u_alu_sl_shiftoneleft_15_result), .RESULT(u_alu_sl_shiftoneleft_16_result));
  u_ALU_SL_SHIFTONELEFT u_alu_sl_shiftoneleft_17 (
    .VALTOSHIFT(u_alu_sl_shiftoneleft_13_result), .RESULT(u_alu_sl_shiftoneleft_17_result));
  u_ALU_SL_SHIFTONELEFT u_alu_sl_shiftoneleft_18 (
    .VALTOSHIFT(u_alu_sl_shiftoneleft_17_result), .RESULT(u_alu_sl_shiftoneleft_18_result));
  Multiplexer #(.width(32)) multiplexer_2 (
    .in0(multiplexer_1_out), .in1(u_alu_sl_shiftoneleft_19_result), .out(multiplexer_2_out), .sel(ALU_Y[1]));  // open: en
  u_ALU_SL_SHIFTONELEFT u_alu_sl_shiftoneleft_19 (
    .VALTOSHIFT(u_alu_sl_shiftoneleft_14_result), .RESULT(u_alu_sl_shiftoneleft_19_result));
  Multiplexer #(.width(32)) multiplexer_3 (
    .in0(CONT), .in1(u_alu_sl_shiftoneleft_16_result), .out(CONT_2), .sel(ALU_Y[3]));  // open: en
  u_ALU_SL_SHIFTONELEFT u_alu_sl_shiftoneleft_20 (
    .VALTOSHIFT(u_alu_sl_shiftoneleft_18_result), .RESULT(u_alu_sl_shiftoneleft_20_result));
  u_ALU_SL_SHIFTONELEFT u_alu_sl_shiftoneleft_21 (
    .VALTOSHIFT(u_alu_sl_shiftoneleft_20_result), .RESULT(u_alu_sl_shiftoneleft_21_result));
  u_ALU_SL_SHIFTONELEFT u_alu_sl_shiftoneleft_22 (
    .VALTOSHIFT(multiplexer_2_out), .RESULT(u_alu_sl_shiftoneleft_22_result));
  u_ALU_SL_SHIFTONELEFT u_alu_sl_shiftoneleft_23 (
    .VALTOSHIFT(u_alu_sl_shiftoneleft_21_result), .RESULT(u_alu_sl_shiftoneleft_23_result));
  u_ALU_SL_SHIFTONELEFT u_alu_sl_shiftoneleft_24 (
    .VALTOSHIFT(u_alu_sl_shiftoneleft_23_result), .RESULT(u_alu_sl_shiftoneleft_24_result));
  u_ALU_SL_SHIFTONELEFT u_alu_sl_shiftoneleft_25 (
    .VALTOSHIFT(u_alu_sl_shiftoneleft_26_result), .RESULT(u_alu_sl_shiftoneleft_25_result));
  u_ALU_SL_SHIFTONELEFT u_alu_sl_shiftoneleft_26 (
    .VALTOSHIFT(u_alu_sl_shiftoneleft_22_result), .RESULT(u_alu_sl_shiftoneleft_26_result));
  u_ALU_SL_SHIFTONELEFT u_alu_sl_shiftoneleft_27 (
    .VALTOSHIFT(u_alu_sl_shiftoneleft_24_result), .RESULT(u_alu_sl_shiftoneleft_27_result));
  u_ALU_SL_SHIFTONELEFT u_alu_sl_shiftoneleft_28 (
    .VALTOSHIFT(u_alu_sl_shiftoneleft_27_result), .RESULT(u_alu_sl_shiftoneleft_28_result));
  u_ALU_SL_SHIFTONELEFT u_alu_sl_shiftoneleft_29 (
    .VALTOSHIFT(u_alu_sl_shiftoneleft_25_result), .RESULT(u_alu_sl_shiftoneleft_29_result));
  u_ALU_SL_SHIFTONELEFT u_alu_sl_shiftoneleft_30 (
    .VALTOSHIFT(u_alu_sl_shiftoneleft_28_result), .RESULT(u_alu_sl_shiftoneleft_30_result));
  u_ALU_SL_SHIFTONELEFT u_alu_sl_shiftoneleft_31 (
    .VALTOSHIFT(u_alu_sl_shiftoneleft_30_result), .RESULT(u_alu_sl_shiftoneleft_31_result));
  Multiplexer #(.width(32)) multiplexer_4 (
    .in0(multiplexer_2_out), .in1(u_alu_sl_shiftoneleft_29_result), .out(CONT), .sel(ALU_Y[2]));  // open: en
  Multiplexer #(.width(32)) multiplexer_5 (
    .in0(CONT_2), .in1(u_alu_sl_shiftoneleft_31_result), .out(RESULT), .sel(ALU_Y[4]));  // open: en

  // Other names for the same wires on the sheet: SHIFT_1 = ALU_Y[0]; SHIFT_2 = ALU_Y[1]; SHIFT_4 = ALU_Y[2];
  //   SHIFT_8 = ALU_Y[3]; SHIFT_16 = ALU_Y[4]
endmodule

module u_ALU_SL_SHIFTONELEFT (
  input  [31:0] VALTOSHIFT,
  output [31:0] RESULT
);


  assign RESULT = {VALTOSHIFT[30:0], VALTOSHIFT[0]};
endmodule

module u_ALU_SR (
  input  [31:0] ALU_X,
  input  [31:0] ALU_Y,
  output [31:0] RESULT
);

  Shifter #(.width(32), .shift("ar")) shifter_1 (.in(ALU_X), .\dist (ALU_Y[4:0]), .out(RESULT));
endmodule

module u_ALU_AND (
  input  [31:0] ALU_X,
  input  [31:0] ALU_Y,
  output [31:0] RESULT
);

  assign RESULT = ALU_X & ALU_Y;  // AND_Gate and_1, 32 bits wide
endmodule

module u_ALU_OR (
  input  [31:0] ALU_X,
  input  [31:0] ALU_Y,
  output [31:0] RESULT
);

  assign RESULT = ALU_X | ALU_Y;  // OR_Gate or_1, 32 bits wide
endmodule

module u_ALU_XOR (
  input  [31:0] ALU_X,
  input  [31:0] ALU_Y,
  output [31:0] RESULT
);

  assign RESULT = ALU_X ^ ALU_Y;  // XOR_Gate xor_1, 32 bits wide
endmodule

module u_ALU_DIVIDE (
  input  [31:0] ALU_X,
  input  [31:0] ALU_Y,
  output [31:0] RESULT
);

  wire CHECK, EQ, GT, LT, undriven;
  wire [31:0] demultiplexer_1_out0, demultiplexer_1_out1, multiplexer_1_out, multiplexer_2_out, RESULTREG,
       RESULTSPEC;

  Demultiplexer #(.width(32)) demultiplexer_1 (
    .out0(demultiplexer_1_out0), .out1(demultiplexer_1_out1), .in(ALU_Y), .sel(CHECK), .en(undriven));
  Comparator #(.width(32)) comparator_1 (.a({32{1'b0}}), .b(ALU_Y), .eq(CHECK));  // open: gt, lt
  Comparator #(.width(32)) comparator_2 (.a({32{1'b0}}), .b(ALU_X), .gt(LT), .eq(EQ), .lt(GT));
  Divider #(.width(32)) divider_1 (.a(ALU_X), .b(demultiplexer_1_out0), .out(RESULTREG));  // open: upper, rem
  Multiplexer #(.width(32)) multiplexer_1 (
    .in0(demultiplexer_1_out1), .in1({32{1'b0}}), .out(multiplexer_1_out), .sel(EQ));  // open: en
  Multiplexer #(.width(32)) multiplexer_2 (
    .in0(multiplexer_1_out), .in1(32'h7fffffff), .out(multiplexer_2_out), .sel(GT));  // open: en
  Multiplexer #(.width(32)) multiplexer_3 (
    .in0(multiplexer_2_out), .in1(32'h80000000), .out(RESULTSPEC), .sel(LT));  // open: en
  Multiplexer #(.width(32)) multiplexer_4 (.in0(RESULTREG), .in1(RESULTSPEC), .out(RESULT), .sel(CHECK));  // open: en
endmodule

module u_ALU_STU (
  input  [31:0] ALU_X,
  input  [31:0] ALU_Y,
  output [31:0] RESULT
);


  assign RESULT = {ALU_Y[16:0], ALU_X[14:0]};

  // Notes on the sheet:
  //   Get Lower 17 bits (Actual Immediate)
endmodule
